# Fritzing sketch sensor-lcd (saved by Fritzing 1.0.6)
breadboards: 1

parts:
  Mod1 = Raspberry Pi Pico W
  Sensor_with_Analog_Out = 6mm Trimmer Potentiometer [maximum_resistance=10kΩ knob_status=50% power=0.5W package=THT]
  R2 = Resistor [tolerance=±5% power=0.25W resistance=10k package=THT]
  R3 = Resistor [tolerance=±5% power=0.25W resistance=20k package=THT]
  LCM1602_IIC1 = LCM1602 IIC [part_number="LCM1602 IIC" chip_label="LCM1602 IIC" package="DIP (Dual Inline) [THT]"]
  V1 = DC Power [voltage=5V internal_resistance=0.1Ω]
  V2 = DC Power [voltage=3.3V internal_resistance=0.1Ω]
  C1 = Ceramic Capacitor [capacitance=100nF voltage=35V package="100 mil [THT, multilayer]"]
  RHT1 = Humidity and Temperature Sensor RHT03

nets:
  N1: Mod1.pin_1, RHT1.Data-signal
  GND: Mod1.pin_3, Mod1.pin_33, Mod1.pin_38, Sensor_with_Analog_Out.leg2, R3.Pin_1, LCM1602_IIC1.GND, C1.0, RHT1.GND_2
  N2: Mod1.pin_6, LCM1602_IIC1.SDA
  N3: Mod1.pin_7, LCM1602_IIC1.SCL
  N4: Mod1.pin_31, R2.Pin_1, R3.Pin_0, C1.1
  N5: Mod1.pin_39, Sensor_with_Analog_Out.leg1, V1.V-
  N6: Sensor_with_Analog_Out.wiper, R2.Pin_0
  VCC: LCM1602_IIC1.VCC, V2.V-, RHT1.Vcc

notes:
  3.3v max to ADC

custom parts:
  Raspberry Pi Pico W: Raspberry Pi Pico W. Based around the RP2040 microcontroller the Pico W is a low cost microcontroller device bringing Raspberry Pi quality, cost, and easy of use to the microcontroller space. The areas marked KEEPOUT in pcb silkscreen should not have traces running through them to avoid shorts on a soldered in module!
  LCM1602 IIC: I2C-Module to use a 1602 or 2004 LCD on with the wire.h libory Serial LCD Modul
